# Fritzing sketch velocista (saved by Fritzing 0.9.3b)
circuit board: 9cm x 8cm
breadboards: 1

parts:
  Encoder_2 = Generic male header - 4 pins [form="♂ (male)" package=THT]
  Encoder_1 = Generic male header - 4 pins [form="♂ (male)" package=THT]
  Multiplexor = Analog Digital MUX Breakout
  Buzzer = Piezo Speaker - PC Mount [part_number=COM-07950]
  Boton_1 = Pushbutton [package=THT]
  Res_1 = Resistor [tolerance=±5% resistance=220 package=THT]
  LED_2 = LED - 5mm [color="Red (633nm)" package="5 mm [THT]"]
  LED_1 = LED - 5mm [color="Red (633nm)" package="5 mm [THT]"]
  Boton_2 = Pushbutton [package=THT]
  Res_2 = Resistor [tolerance=±5% resistance=220 package=THT]
  J1 = male pin header, 6 pins [form="♂ (male)"]
  J2 = male pin header, 8 pins [form="♂ (male)"]
  J3 = male pin header, 8 pins [form="♂ (male)"]
  J4 = male pin header, 10 pins [form="♂ (male)"]

nets:
  GND: Encoder_2.GND, Encoder_1.GND, Buzzer.GND, J4.pin4
  N1: Encoder_2.OUT_B, J3.pin3
  N2: Encoder_2.OUT_A, J3.pin5
  VCC: Encoder_2.VCC, Encoder_1.VCC, Multiplexor.VCC, Boton_1.leg0, Boton_2.leg0, J2.pin5
  N3: Encoder_1.OUT_B, J3.pin4
  N4: Encoder_1.OUT_A, J3.pin6
  N5: Multiplexor.GND, Multiplexor.EN, J2.pin6
  N6: Multiplexor.S0, J3.pin2
  N7: Multiplexor.S1, J4.pin7
  N8: Multiplexor.S2, J4.pin6
  N9: Multiplexor.S3, J4.pin5
  N10: Multiplexor.SIG, J1.pin1
  N11: Buzzer.VCC, J1.pin2
  N12: Boton_1.leg1, Res_1.Pin_0, J1.pin6
  N13: Res_1.Pin_1, LED_2.cathode, LED_1.cathode, Res_2.Pin_0, J2.pin7
  N14: LED_2.anode, J1.pin4
  N15: LED_1.anode, J1.pin5
  N16: Boton_2.leg1, Res_2.Pin_1, J1.pin3

notes:
  El Retorno De Bob II

custom parts:
  Generic male header - 4 pins: Generic male header
  Piezo Speaker - PC Mount: This is a small 12mm round speaker that operates around the audible 2kHz range. You can use these speakers to create simple music or user interfaces. Each speaker is PTH solderable and requires an operating voltage of 3.5-5V with a mean current of 35mA max. These speakers also have a typical sound output of 95 dBA and a coil resistance of 42 ±6.3 ohms.
